// Logisim project IT012_Lab01_25520138.circ as structural Verilog: 6 circuits, main circuit warm up
module warm_up (
  input  in_1,
  input  in_2,
  output out_3
);

  wire not_1_out;

  not not_1 (not_1_out, in_2);
  and and_1 (out_3, in_1, not_1_out);
endmodule

module TN1 (
  input  A,
  input  B,
  input  c,
  output out_4,
  output out_5,
  output out_6,
  output out_7,
  output out_8,
  output out_9,
  output out_10,
  output out_11,
  output out_12,
  output out_13
);

  not A_prime (out_4, A);
  and and_1 (out_5, A, B);
  or or_1 (out_6, A, B);
  nand nand_1 (out_7, A, B);
  nor nor_1 (out_9, A, B);
  xor xor_1 (out_10, A, B);
  xnor xnor_1 (out_11, A, B);
  xor XOR3 (out_12, A, B, c);
  nand NAND3 (out_13, A, B, c);
  nand CHAIN (out_8, out_7, c);
endmodule

module TN2 (
  input  x,
  input  y,
  input  z,
  output EQ1,
  output EQ2,
  output EQ3,
  output EQ4,
  output EQ5
);

  wire and_1_out, and_2_out, and_3_out, and_4_out, nand_1_out, nor_1_out, not_1_out, not_2_out, or_1_out,
       or_2_out, or_3_out, or_4_out;

  not not_1 (not_1_out, x);
  not not_2 (not_2_out, y);
  and and_1 (and_1_out, not_1_out, not_2_out);
  and and_2 (and_2_out, y, z);
  nor nor_1 (nor_1_out, x, y);
  nand nand_1 (nand_1_out, x, y);
  or or_1 (or_1_out, x, y);
  or or_2 (or_2_out, x, z);
  and and_3 (and_3_out, not_1_out, y);
  or or_3 (or_3_out, and_2_out, x);
  and and_4 (and_4_out, or_1_out, or_2_out);
  or or_4 (or_4_out, x, and_3_out);
  xnor xnor_1 (EQ1, nor_1_out, and_1_out);
  xnor xnor_2 (EQ2, and_1_out, nand_1_out);
  xnor xnor_3 (EQ3, or_3_out, and_4_out);
  xnor xnor_4 (EQ4, or_4_out, x);
  xnor xnor_5 (EQ5, or_4_out, or_1_out);
endmodule

module TN3 (
  input  A,
  input  B,
  input  C,
  input  D,
  output F
);

  wire and_1_out, and_2_out, and_3_out, and_4_out, and_5_out, and_6_out, not_1_out, not_2_out, not_3_out,
       not_4_out;

  not not_1 (not_1_out, A);
  not not_2 (not_2_out, B);
  not not_3 (not_3_out, C);
  not not_4 (not_4_out, D);
  and and_1 (and_1_out, not_1_out, not_2_out, C, not_4_out);
  and and_2 (and_2_out, not_1_out, not_2_out, C, D);
  and and_3 (and_3_out, not_1_out, B, not_3_out, D);
  and and_4 (and_4_out, not_1_out, B, C, D);
  and and_5 (and_5_out, A, not_2_out, C, D);
  and and_6 (and_6_out, A, B, not_3_out, D);
  or or_1 (F, and_1_out, and_2_out, and_3_out, and_4_out, and_5_out, and_6_out);
endmodule

module TN4 (
  input  A,
  input  B,
  input  C,
  input  D,
  output F_can,
  output EQ1,
  output EQ2
);

  wire and_1_out, and_2_out, and_3_out, and_4_out, and_5_out, and_6_out, and_7_out, and_8_out, and_9_out,
       and_10_out, and_11_out, F_sop_out, not_1_out, not_2_out, not_3_out, not_4_out, or_1_out, or_2_out,
       or_3_out, or_4_out;

  not not_1 (not_1_out, A);
  not not_2 (not_2_out, B);
  not not_3 (not_3_out, C);
  not not_4 (not_4_out, D);
  and and_1 (and_1_out, not_1_out, not_2_out, C, not_4_out);
  and and_2 (and_2_out, not_1_out, not_2_out, C, D);
  and and_3 (and_3_out, not_1_out, B, not_3_out, D);
  and and_4 (and_4_out, not_1_out, B, C, D);
  and and_5 (and_5_out, A, not_2_out, C, D);
  and and_6 (and_6_out, A, B, not_3_out, D);
  and and_7 (and_7_out, not_1_out, not_2_out, C);
  and and_8 (and_8_out, not_2_out, C, D);
  and and_9 (and_9_out, not_1_out, B, D);
  and and_10 (and_10_out, B, not_3_out, D);
  or or_1 (or_1_out, not_1_out, D);
  or or_2 (or_2_out, B, C);
  or or_3 (or_3_out, not_2_out, D);
  or or_4 (or_4_out, not_1_out, not_2_out, not_3_out);
  or u_F_can (F_can, and_1_out, and_2_out, and_3_out, and_4_out, and_5_out, and_6_out);
  or F_sop (F_sop_out, and_7_out, and_8_out, and_9_out, and_10_out);
  and and_11 (and_11_out, or_1_out, or_2_out, or_3_out, or_4_out);
  xnor xnor_1 (EQ1, F_can, F_sop_out);
  xnor xnor_2 (EQ2, F_sop_out, and_11_out);
endmodule

module TN5 (
  input  A,
  input  B,
  input  C,
  output F
);

  wire xor_1_out;

  xor xor_1 (xor_1_out, A, B);
  xor xor_2 (F, xor_1_out, C);
endmodule
